// Logisim project pongocpu.circ as structural Verilog: 1 circuit, main circuit main
module main (
);

  wire and_1_out, and_2_out, and_3_out, and_4_out, and_5_out, and_6_out, and_7_out, clock_1_out,
       comparator_1_gt, decoder_1_out0, decoder_1_out1, decoder_1_out2, decoder_1_out3, demultiplexer_1_out0,
       demultiplexer_1_out1, demultiplexer_1_out2, demultiplexer_1_out3, demultiplexer_1_out10,
       demultiplexer_1_out11, demultiplexer_1_out12, demultiplexer_1_out13, demultiplexer_1_out14, not_1_out,
       not_2_out, not_3_out, or_1_out, or_2_out, or_3_out, or_4_out, or_5_out, or_6_out, or_7_out,
       pull_resistor_1_node, rgb_video_1_p1, Rst_out, s_r_ff_1_qn;
  wire [1:0] counter_1_q;
  wire [3:0] ThisInst_q, ThisInst_q_3;
  wire [4:0] Dx_q, Dy_q, joystick_1_x, joystick_1_y;
  wire [7:0] adder_1_out, bit_extender_3_out, bit_extender_4_out, Col_q, Ip_q, Lp_q, multiplexer_1_out,
       multiplexer_2_out, multiplexer_4_out, not_4_out, OpA_q, OpB_q;
  wire [7:4] ThisInst_q_2;
  wire [7:5] Dx_q_2, Dy_q_2;
  wire [16:0] bit_extender_1_out, bit_extender_2_out, multiplexer_3_out, multiplexer_5_out, ram_1_dout,
       ThisData_q;
  wire [16:12] ThisInst_q_4;

  Decoder #(.enable("false"), .select(2)) decoder_1 (
    .out0(decoder_1_out0), .out1(decoder_1_out1), .out2(decoder_1_out2), .out3(decoder_1_out3),
    .sel(counter_1_q));
  Counter #(.max('h3), .width(2)) counter_1 (
    .Q(counter_1_q), .clk(clock_1_out), .clr(Rst_out));  // open: load, D, count, carry, up
  not not_1 (not_1_out, clock_1_out);
  LED led_1 (.in(multiplexer_2_out[6]));
  LED led_2 (.in(multiplexer_2_out[7]));
  not not_2 (not_2_out, or_6_out);
  and and_1 (and_1_out, not_1_out, decoder_1_out2, not_2_out);
  Demultiplexer #(.select(4)) demultiplexer_1 (
    .out0(demultiplexer_1_out0), .out1(demultiplexer_1_out1), .out2(demultiplexer_1_out2),
    .out3(demultiplexer_1_out3), .out10(demultiplexer_1_out10), .out11(demultiplexer_1_out11),
    .out12(demultiplexer_1_out12), .out13(demultiplexer_1_out13), .out14(demultiplexer_1_out14),
    .in(and_1_out), .sel(ThisInst_q));  // open: out4, out5, out6, out7, out8, out9, out15
  or or_1 (or_1_out, or_2_out, decoder_1_out0);
  and and_2 (and_2_out, or_6_out, decoder_1_out2, not_1_out);
  S_R_Flip_Flop s_r_ff_1 (
    .S(or_2_out), .clk(or_1_out), .R(decoder_1_out0), .Qn(s_r_ff_1_qn), .reset(Rst_out));  // open: Q, preset
  not not_3 (not_3_out, s_r_ff_1_qn);
  and and_3 (and_3_out, demultiplexer_1_out1, not_3_out);
  and and_4 (and_4_out, not_1_out, decoder_1_out0);
  RAM #(.dataWidth(17), .enables("line"), .\type ("nonvolatile")) ram_1 (
    .addr(multiplexer_1_out), .we(decoder_1_out2), .clk(and_2_out), .din(ThisData_q), .dout(ram_1_dout));
  Multiplexer #(.width(8)) multiplexer_1 (
    .in0({ThisInst_q_2, ThisInst_q}), .in1(Ip_q), .out(multiplexer_1_out), .sel(decoder_1_out0));
  Multiplexer #(.width(8)) multiplexer_2 (
    .in0({8{1'b0}}), .in1(ThisData_q[7:0]), .out(multiplexer_2_out), .sel(demultiplexer_1_out13));
  and and_5 (and_5_out, demultiplexer_1_out1, comparator_1_gt);
  and and_6 (and_6_out, decoder_1_out3, not_1_out, s_r_ff_1_qn);
  or or_2 (or_2_out, and_6_out, and_5_out, demultiplexer_1_out0);
  Register #(.width(17)) ThisInst (
    .D(ram_1_dout), .Q({ThisInst_q_4, ThisInst_q_3, ThisInst_q_2, ThisInst_q}), .clk(and_4_out), .clr(Rst_out));  // open: en
  Counter Ip (
    .load(decoder_1_out2), .D(ThisData_q[7:0]), .Q(Ip_q), .clk(or_2_out), .clr(Rst_out));  // open: count, carry, up
  Register OpA (.D(ThisData_q[7:0]), .Q(OpA_q), .clk(demultiplexer_1_out2), .clr(Rst_out));  // open: en
  Register OpB (.D(ThisData_q[7:0]), .Q(OpB_q), .clk(demultiplexer_1_out3), .clr(Rst_out));  // open: en
  Counter Dx (
    .load(demultiplexer_1_out10), .D(ThisData_q[7:0]), .Q({Dx_q_2, Dx_q}), .clk(or_3_out), .clr(Rst_out));  // open: count, carry, up
  or or_3 (or_3_out, demultiplexer_1_out10, multiplexer_2_out[0]);
  Counter Dy (
    .load(demultiplexer_1_out11), .D(ThisData_q[7:0]), .Q({Dy_q_2, Dy_q}), .clk(or_4_out), .clr(Rst_out));  // open: count, carry, up
  or or_4 (or_4_out, demultiplexer_1_out11, multiplexer_2_out[1]);
  Register Col (.D(ThisData_q[7:0]), .Q(Col_q), .clk(demultiplexer_1_out12), .clr(Rst_out));  // open: en
  Pull_Resistor pull_resistor_1 (.node(pull_resistor_1_node));
  Counter Lp (
    .load(demultiplexer_1_out14), .D(ThisData_q[7:0]), .Q(Lp_q), .up(pull_resistor_1_node), .clk(or_5_out),
    .clr(Rst_out));  // open: count, carry
  or or_5 (or_5_out, demultiplexer_1_out14, and_3_out, multiplexer_2_out[4]);
  or or_6 (or_6_out, ThisInst_q_2[4], ThisInst_q_2[5], ThisInst_q_2[6], ThisInst_q_2[7]);
  assign not_4_out = ~OpA_q;  // NOT_Gate not_4, 8 bits wide
  Adder adder_1 (.a(OpA_q), .b(OpB_q), .out(adder_1_out));  // open: cin, cout
  Comparator comparator_1 (.a(Lp_q), .b({8{1'b0}}), .gt(comparator_1_gt));  // open: eq, lt
  or or_7 (or_7_out, ThisInst_q_4[12], ThisInst_q_4[13], ThisInst_q_4[14], ThisInst_q_4[15]);
  Multiplexer #(.width(17)) multiplexer_3 (
    .in0(bit_extender_2_out), .in1(ram_1_dout), .out(multiplexer_3_out), .sel(or_7_out));
  assign bit_extender_1_out = {{9{ThisInst_q_4[15]}}, {ThisInst_q_4[15:12], ThisInst_q_3}};  // Bit_Extender bit_extender_1
  Multiplexer #(.select(4), .width(8)) multiplexer_4 (
    .in0(Ip_q), .in1(Ip_q), .in2(OpA_q), .in3(OpB_q), .in4(adder_1_out), .in5(not_4_out), .in6({8{1'b0}}),
    .in7({8{1'b0}}), .in8(bit_extender_4_out), .in9(bit_extender_3_out), .in10({Dx_q_2, Dx_q}),
    .in11({Dy_q_2, Dy_q}), .in12(Col_q), .in13({8{1'b0}}), .in14(Lp_q), .in15({8{1'b0}}),
    .out(multiplexer_4_out), .sel(ThisInst_q_3));
  Multiplexer #(.width(17)) multiplexer_5 (
    .in0(multiplexer_3_out), .in1(bit_extender_1_out), .out(multiplexer_5_out), .sel(ThisInst_q_4[16]));
  and and_7 (and_7_out, decoder_1_out1, not_1_out);
  assign bit_extender_2_out = {{9{multiplexer_4_out[7]}}, multiplexer_4_out};  // Bit_Extender bit_extender_2
  Clock clock_1 (.out(clock_1_out));
  Button Rst (.out(Rst_out));
  Register #(.width(17)) ThisData (.D(multiplexer_5_out), .Q(ThisData_q), .clk(and_7_out), .clr(Rst_out));  // open: en
  Button button_1 ();  // open: out
  // RGB_Video #(.cursor("No Cursor"), .height(32), .scale(8), .width(32)) rgb_video_1: pin names not known; wires that end beside it: rgb_video_1_p1, multiplexer_2_out[2], multiplexer_2_out[2], Dx_q, Dy_q, Col_q
  or or_8 (rgb_video_1_p1, multiplexer_2_out[3], Rst_out);
  assign bit_extender_3_out = {{3{1'b0}}, joystick_1_x};  // Bit_Extender bit_extender_3
  assign bit_extender_4_out = {{3{1'b0}}, joystick_1_y};  // Bit_Extender bit_extender_4
  Joystick #(.bits(5)) joystick_1 (.x(joystick_1_x), .y(joystick_1_y));
  Joystick joystick_2 ();  // open: x, y
endmodule
