// Logisim project pongofour.circ as structural Verilog: 2 circuits, main circuit main
module main (
);

  wire adder_2_cout, and_1_out, and_2_out, and_3_out, and_4_out, and_5_out, and_6_out, buffer_1_out,
       buffer_2_out, button_1_out, button_2_out, button_3_out, button_4_out, button_5_out, button_6_out,
       button_7_out, clock_1_out, comparator_1_gt, d_ff_1_q, d_ff_1_qn, d_ff_2_q, d_ff_2_qn, decoder_1_out0,
       decoder_1_out1, decoder_1_out2, decoder_1_out3, decoder_1_out4, decoder_1_out7, decoder_1_out8,
       decoder_1_out12, decoder_1_out13, decoder_1_out14, decoder_1_out15, decoder_2_out0, decoder_2_out1,
       decoder_2_out2, decoder_2_out3, decoder_2_out4, decoder_2_out5, decoder_2_out6, decoder_2_out7,
       decoder_3_out0, decoder_3_out1, decoder_3_out2, decoder_3_out3, decoder_3_out4, decoder_3_out5,
       decoder_3_out6, decoder_3_out7, IndiLo_carry, IpLo_carry, j_k_ff_1_q, j_k_ff_1_qn, j_k_ff_2_q,
       j_k_ff_2_qn, LoopLo_carry, not_1_out, not_2_out, not_3_out, not_5_out, not_6_out, or_1_out, or_2_out,
       or_3_out, pull_resistor_1_node, pull_resistor_2_node, pull_resistor_3_node, pull_resistor_4_node,
       s_r_ff_1_q, s_r_ff_2_q, s_r_ff_2_qn, s_r_ff_3_q, s_r_ff_3_qn, s_r_ff_4_q, s_r_ff_4_qn, t_ff_1_q,
       t_ff_1_qn, undriven, undriven_2, undriven_4;
  wire [2:0] undriven_3;
  wire [3:0] PushHi_q;
  wire [4:0] joystick_1_x, joystick_1_y, rgb_video_1_p4, rgb_video_1_p5;
  wire [5:0] Inst_q_2, PushLo_q;
  wire [5:4] PushHi_q_2;
  wire [7:0] adder_2_out, controlled_buffer_1_out, controlled_buffer_7_out, IndiHi_q, IndiLo_q, LoopHi_q,
       LoopLo_q, nand_2_out, OpA_q, OpB_q, ram_1_dout, register_3_q, register_6_q, register_7_q,
       rgb_video_1_p6, rom_1_data, undriven_5, WasCarry_q;
  wire [7:6] Inst_q;
  wire [15:0] adder_1_out, bit_extender_4_out, bit_extender_5_out, bit_extender_6_out, divider_1_out,
       divider_1_rem, Ip_q, IpLo_q, multiplexer_1_out, multiplexer_2_out, multiplexer_3_out, nand_1_out,
       ram_2_dout, RamAddr_q, register_1_q, register_2_q, register_4_q, register_5_q, rom_2_data, Test_q,
       TmpA_q, TmpB_q, TmpC_q;

  Shift_Register #(.length(16)) shift_register_1 ();  // open: shift, in, clk, out, load, clr, d0, q0, d1, q1, d2, q2, d3, q3, d4, q4, d5, q5, d6, q6, d7, q7, d8, q8, d9, q9, d10, q10, d11, q11, d12, q12, d13, q13, d14, q14, d15, q15
  RAM #(.addrWidth(16), .trigger("high")) ram_1 (.addr(IpLo_q), .dout(ram_1_dout));  // open: we, oe, din
  Clock clock_1 (.out(clock_1_out));
  Pull_Resistor #(.pull(1)) pull_resistor_1 (.node(pull_resistor_1_node));
  not not_1 (not_1_out, clock_1_out);
  Button button_1 (.out(button_1_out));
  Decoder #(.enable("false"), .select(4)) decoder_1 (
    .out0(decoder_1_out0), .out1(decoder_1_out1), .out2(decoder_1_out2), .out3(decoder_1_out3),
    .out4(decoder_1_out4), .out7(decoder_1_out7), .out8(decoder_1_out8), .out12(decoder_1_out12),
    .out13(decoder_1_out13), .out14(decoder_1_out14), .out15(decoder_1_out15), .sel(register_4_q[4:1]));  // open: out5, out6, out9, out10, out11
  and and_1 (and_1_out, t_ff_1_q, not_1_out);
  T_Flip_Flop t_ff_1 (
    .clk(clock_1_out), .T(pull_resistor_1_node), .Q(t_ff_1_q), .Qn(t_ff_1_qn), .reset(button_1_out));  // open: preset
  and and_2 (and_2_out, t_ff_1_qn, not_1_out);
  or or_1 (or_1_out, decoder_1_out0, and_3_out);
  and and_3 (and_3_out, decoder_1_out1, comparator_1_gt);
  Button button_2 (.out(button_2_out));
  not not_2 (not_2_out, button_2_out);
  ROM rom_1 (.addr(register_3_q), .data(rom_1_data));
  ROM #(.addrWidth(16), .dataWidth(16)) rom_2 (.addr(Ip_q), .data(rom_2_data));
  Counter #(.max('hffff), .width(16)) Ip (
    .load(or_1_out), .D(register_5_q), .Q(Ip_q), .clk(and_1_out), .clr(button_1_out));  // open: count, carry, up
  Register #(.width(16)) Test (.D(register_5_q), .en(decoder_1_out2), .Q(Test_q), .clk(and_1_out), .clr(button_1_out));
  RAM #(.addrWidth(16), .dataWidth(16), .enables("line")) ram_2 (
    .addr(RamAddr_q), .we(decoder_1_out8), .clk(and_1_out), .din(register_5_q), .dout(ram_2_dout));
  Register Inst (.D(ram_1_dout), .Q({Inst_q, Inst_q_2}), .clk(button_2_out), .clr(button_3_out));  // open: en
  Register #(.width(6)) PushLo (.D(Inst_q_2), .en(j_k_ff_1_qn), .Q(PushLo_q), .clk(and_5_out), .clr(button_3_out));
  Register #(.width(6)) PushHi (
    .D(Inst_q_2), .en(j_k_ff_1_q), .Q({PushHi_q_2, PushHi_q}), .clk(and_5_out), .clr(button_3_out));
  Button button_3 (.out(button_3_out));
  Counter IpHi (
    .D(ram_1_dout), .count(IpLo_carry), .Q(IpLo_q[15:8]), .clk(not_2_out), .clr(button_3_out));  // open: load, carry, up
  Counter IpLo (
    .D(ram_1_dout), .Q(IpLo_q[7:0]), .carry(IpLo_carry), .clk(not_2_out), .clr(button_3_out));  // open: load, count, up
  Pull_Resistor pull_resistor_2 (.node(pull_resistor_2_node));
  Counter LoopHi (
    .D(ram_1_dout), .count(LoopLo_carry), .Q(LoopHi_q), .up(pull_resistor_2_node), .clk(undriven),
    .clr(button_3_out));  // open: load, carry
  Pull_Resistor pull_resistor_3 (.node(pull_resistor_3_node));
  Counter LoopLo (
    .D(ram_1_dout), .Q(LoopLo_q), .carry(LoopLo_carry), .up(pull_resistor_3_node), .clk(undriven_2),
    .clr(button_3_out));  // open: load, count
  Counter IndiHi (
    .D(ram_1_dout), .count(IndiLo_carry), .Q(IndiHi_q), .clr(button_3_out));  // open: load, carry, up, clk
  Counter IndiLo (
    .D(ram_1_dout), .Q(IndiLo_q), .carry(IndiLo_carry), .clr(button_3_out));  // open: load, count, up, clk
  Register #(.width(16)) register_1 (
    .D(register_5_q), .en(decoder_1_out3), .Q(register_1_q), .clk(and_1_out), .clr(button_1_out));
  Register #(.width(16)) register_2 (
    .D(register_5_q), .en(decoder_1_out4), .Q(register_2_q), .clk(and_1_out), .clr(button_1_out));
  // RGB_Video #(.height(32), .scale(5), .width(32)) rgb_video_1: pin names not known; wires that end beside it: button_1_out, and_1_out, decoder_1_out8, rgb_video_1_p4, rgb_video_1_p5, rgb_video_1_p6, Inst_q[7], Inst_q[6]
  Bit_Extender #(.in_width(16), .out_width(8)) bit_extender_1 (.in(register_5_q), .out(rgb_video_1_p6));
  Bit_Extender #(.in_width(16), .out_width(5)) bit_extender_2 (.in(divider_1_out), .out(rgb_video_1_p5));
  Divider #(.width(16)) divider_1 (.a(RamAddr_q), .b(16'h20), .out(divider_1_out), .rem(divider_1_rem));  // open: upper
  Bit_Extender #(.in_width(16), .out_width(5)) bit_extender_3 (.in(divider_1_rem), .out(rgb_video_1_p4));
  Pull_Resistor #(.pull(1)) pull_resistor_4 (.node(pull_resistor_4_node));
  Register #(.width(16)) RamAddr (
    .D(register_5_q), .en(decoder_1_out7), .Q(RamAddr_q), .clk(and_1_out), .clr(button_1_out));
  Register #(.width(16)) TmpA (.D(register_5_q), .en(decoder_1_out13), .Q(TmpA_q), .clk(and_1_out), .clr(button_1_out));
  not not_3 (not_3_out, Inst_q[7]);
  // NOT_Gate not_4 has open pins: in=Inst_q[6], out=open
  and and_4 (and_4_out, Inst_q[6], Inst_q[7]);
  not not_5 (not_5_out, and_4_out);
  and and_5 (and_5_out, and_4_out, not_2_out);
  J_K_Flip_Flop j_k_ff_1 (
    .J(pull_resistor_4_node), .clk(button_2_out), .K(pull_resistor_4_node), .Q(j_k_ff_1_q), .Qn(j_k_ff_1_qn),
    .reset(or_2_out));  // open: preset
  or or_2 (or_2_out, j_k_ff_2_qn, button_3_out);
  Decoder #(.select(3)) decoder_2 (
    .out0(decoder_2_out0), .out1(decoder_2_out1), .out2(decoder_2_out2), .out3(decoder_2_out3),
    .out4(decoder_2_out4), .out5(decoder_2_out5), .out6(decoder_2_out6), .out7(decoder_2_out7),
    .sel(undriven_3));  // open: en
  assign controlled_buffer_1_out = decoder_2_out0 ? IpLo_q[15:8] : 8'bz;  // Controlled_Buffer controlled_buffer_1
  assign controlled_buffer_1_out = decoder_2_out1 ? IpLo_q[7:0] : 8'bz;  // Controlled_Buffer controlled_buffer_2
  assign controlled_buffer_1_out = decoder_2_out2 ? LoopHi_q : 8'bz;  // Controlled_Buffer controlled_buffer_3
  assign controlled_buffer_1_out = decoder_2_out3 ? LoopLo_q : 8'bz;  // Controlled_Buffer controlled_buffer_4
  assign controlled_buffer_1_out = decoder_2_out4 ? IndiHi_q : 8'bz;  // Controlled_Buffer controlled_buffer_5
  assign controlled_buffer_1_out = decoder_2_out5 ? IndiLo_q : 8'bz;  // Controlled_Buffer controlled_buffer_6
  Adder #(.width(16)) adder_1 (.a(register_1_q), .b(register_2_q), .out(adder_1_out));  // open: cin, cout
  Register #(.width(16)) TmpB (.D(register_5_q), .en(decoder_1_out14), .Q(TmpB_q), .clk(and_1_out), .clr(button_1_out));
  Register #(.width(16)) TmpC (.D(register_5_q), .en(decoder_1_out15), .Q(TmpC_q), .clk(and_1_out), .clr(button_1_out));
  J_K_Flip_Flop j_k_ff_2 (
    .J(and_4_out), .clk(not_2_out), .K(not_5_out), .Q(j_k_ff_2_q), .Qn(j_k_ff_2_qn), .reset(button_3_out));  // open: preset
  Register register_3 (.D(rom_1_data), .Q(register_3_q), .clk(button_4_out));  // open: en, clr
  Button button_4 (.out(button_4_out));
  Register #(.width(16)) register_4 (
    .D(rom_2_data), .Q(register_4_q), .clk(and_2_out), .clr(button_1_out));  // open: en
  assign nand_1_out = ~(register_1_q & register_2_q);  // NAND_Gate nand_1, 16 bits wide
  Comparator #(.width(16)) comparator_1 (.a(Test_q), .b({16{1'b0}}), .gt(comparator_1_gt));  // open: eq, lt
  Register OpA (.D(ram_1_dout), .Q(OpA_q), .clr(button_3_out));  // open: en, clk
  Register OpB (.D(ram_1_dout), .Q(OpB_q), .clr(button_3_out));  // open: en, clk
  assign controlled_buffer_7_out = decoder_3_out4 ? ram_1_dout : 8'bz;  // Controlled_Buffer controlled_buffer_7
  assign bit_extender_4_out = {{5{register_4_q[15]}}, register_4_q[15:5]};  // Bit_Extender bit_extender_4
  Multiplexer #(.select(4), .width(16)) multiplexer_1 (
    .in0(Ip_q), .in1(Ip_q), .in2(Test_q), .in3(register_1_q), .in4(register_2_q), .in5(adder_1_out),
    .in6(nand_1_out), .in7(RamAddr_q), .in8({16{1'b0}}), .in9(ram_2_dout), .in10(bit_extender_5_out),
    .in11(bit_extender_6_out), .in12({16{1'b0}}), .in13(TmpA_q), .in14(TmpB_q), .in15(TmpC_q),
    .out(multiplexer_1_out), .sel(register_4_q[8:5]));
  Joystick #(.bits(5)) joystick_1 (.x(joystick_1_x), .y(joystick_1_y));
  assign nand_2_out = ~(OpA_q & OpB_q);  // NAND_Gate nand_2, 8 bits wide
  Adder adder_2 (.a(OpA_q), .b(OpB_q), .out(adder_2_out), .cin(WasCarry_q[0]), .cout(adder_2_cout));
  buf buffer_1 (buffer_1_out, adder_2_cout);
  S_R_Flip_Flop #(.trigger("high")) WasCarry (
    .S(buffer_1_out), .clk(or_3_out), .R(buffer_2_out), .Q(WasCarry_q[0]), .reset(button_3_out));  // open: Qn, preset
  or or_3 (or_3_out, buffer_1_out, buffer_2_out);
  buf buffer_2 (buffer_2_out, controlled_buffer_7_out[0]);
  Multiplexer #(.width(16)) multiplexer_2 (
    .in0(multiplexer_1_out), .in1(multiplexer_3_out), .out(multiplexer_2_out), .sel(register_4_q[0]));
  assign bit_extender_5_out = {{11{joystick_1_x[4]}}, joystick_1_x};  // Bit_Extender bit_extender_5
  assign bit_extender_6_out = {{11{joystick_1_y[4]}}, joystick_1_y};  // Bit_Extender bit_extender_6
  Register DataLo (.D({PushLo_q[1:0], Inst_q_2}), .en(not_3_out), .clk(not_2_out), .clr(button_3_out));  // open: Q
  Register DataHi (.D({PushHi_q, PushLo_q[5:2]}), .en(not_3_out), .clk(not_2_out), .clr(button_3_out));  // open: Q
  Decoder #(.select(3)) decoder_3 (
    .out0(decoder_3_out0), .out1(decoder_3_out1), .out2(decoder_3_out2), .out3(decoder_3_out3),
    .out4(decoder_3_out4), .out5(decoder_3_out5), .out6(decoder_3_out6), .out7(decoder_3_out7),
    .sel(undriven_3));  // open: en
  assign controlled_buffer_1_out = decoder_3_out0 ? OpA_q : 8'bz;  // Controlled_Buffer controlled_buffer_8
  assign controlled_buffer_1_out = decoder_3_out1 ? OpB_q : 8'bz;  // Controlled_Buffer controlled_buffer_9
  assign controlled_buffer_1_out = decoder_3_out2 ? nand_2_out : 8'bz;  // Controlled_Buffer controlled_buffer_10
  assign controlled_buffer_1_out = decoder_3_out3 ? adder_2_out : 8'bz;  // Controlled_Buffer controlled_buffer_11
  assign controlled_buffer_1_out = decoder_3_out4 ? WasCarry_q : 8'bz;  // Controlled_Buffer controlled_buffer_12
  Multiplexer #(.width(16)) multiplexer_3 (
    .in0(bit_extender_4_out), .in1({register_4_q[15:5], {5{1'b0}}}), .out(multiplexer_3_out), .sel(s_r_ff_1_q));
  Register #(.width(16)) register_5 (
    .D(multiplexer_2_out), .Q(register_5_q), .clk(t_ff_1_q), .clr(button_1_out));  // open: en
  S_R_Flip_Flop s_r_ff_1 (
    .S(register_5_q[2]), .R(register_5_q[1]), .clk(decoder_1_out12), .Q(s_r_ff_1_q));  // open: reset, Qn, preset
  Button button_5 (.out(button_5_out));
  S_R_Flip_Flop s_r_ff_2 (
    .S(s_r_ff_4_q), .clk(button_5_out), .R(s_r_ff_4_qn), .Q(s_r_ff_2_q), .Qn(s_r_ff_2_qn),
    .preset(button_6_out));  // open: reset
  S_R_Flip_Flop s_r_ff_3 (
    .S(s_r_ff_2_q), .clk(button_5_out), .R(s_r_ff_2_qn), .Q(s_r_ff_3_q), .Qn(s_r_ff_3_qn),
    .reset(button_6_out));  // open: preset
  S_R_Flip_Flop s_r_ff_4 (
    .S(s_r_ff_3_q), .clk(button_5_out), .R(s_r_ff_3_qn), .Q(s_r_ff_4_q), .Qn(s_r_ff_4_qn),
    .reset(button_6_out));  // open: preset
  Button button_6 (.out(button_6_out));
  Register register_6 (.D(undriven_5), .en(d_ff_1_qn), .Q(register_6_q), .clk(undriven_4), .clr(button_7_out));
  Register register_7 (.D(undriven_5), .en(and_6_out), .Q(register_7_q), .clk(undriven_4), .clr(button_7_out));
  Register register_8 (.D(undriven_5), .en(d_ff_2_q), .clk(undriven_4), .clr(button_7_out));  // open: Q
  Button button_7 (.out(button_7_out));
  and and_6 (and_6_out, d_ff_2_qn, d_ff_1_q);
  not not_6 (not_6_out, undriven_4);
  D_Flip_Flop d_ff_1 (
    .clk(not_6_out), .D(register_6_q[7]), .Q(d_ff_1_q), .Qn(d_ff_1_qn), .reset(button_7_out));  // open: preset
  D_Flip_Flop d_ff_2 (
    .clk(not_6_out), .D(register_7_q[7]), .Q(d_ff_2_q), .Qn(d_ff_2_qn), .reset(button_7_out));  // open: preset

  // Notes on the sheet:
  //   contents of rom_1 (hex, n*v repeats v):
  //   2 0 5
  //   contents of rom_2 (hex, n*v repeats v):
  //   800f d1 802f d1 810f d1 812f 511 808f 31 80af 31 804f 211 808f 126 128 c6 29 b0 80cf 151 806f 211
  //   80af 126 128 c6 29 b0 80ef b1 45f 1261 49f 1361 285 ffe9 46 a4 39 4c3 1b 3d 810f 5ff 1781 812f 3dd
  //   67f 1781 6bf 1c61 11 810f 150 812f 170 1ffb 3d 810f 7ff 1781 812f 3dd 87f 1781 80ef 126 ffe9 a4 b0
  //   c03 b1 806f 126 ff89 a4 a03 aa1 126 fc49 a4 aa3 b61 80af 126 128 c6 29 b0 80af 128 806f 126 b0 80cf
  //   126 ffe9 a4 b0 fc3 151 804f 124 de3 800f 126 ffe9 b0 181 126 fc49 a4 e83 f21 802f 126 ffe9 b0 181
  //   808f 128 804f 126 b0 101f 1c61 124 1063 1201 808f 126 128 c6 29 b0 808f 128 804f 126 b0 121f 1c61
  //   1ff1 39 541 7fe5 ffe9 4e 11 46 a4 12a3 1e0 c2f 3c5 1e11 e6 29 ae 46 ffe9 a4 13a3 800f 124 42f 1e11
  //   e6 49 ae 46 ffe9 a4 1503 802f 124 7cf 1e11 e6 ffc9 ae 46 ffe9 a4 1663 1e0 126 89 a6 fca9 a4 1883 64
  //   1981 6e 46 48 c6 29 a8 e6 a4 46 48 a6 68 a6 68 a6 68 a6 68 a6 1c8 ae a5 1b0 e6 409 ae 46 ffe9 a4
  //   1b43 1e0 804f 13a 806f 13c 1c6 1c8 a6 68 a6 68 a6 68 a6 68 a6 1a8 ae 1e0
  //   pushed 1
  //   pushed 2
  //   magic sign extend
  //   goes here
  //   extend sign auto via pushes
  //   x377: octal d-type with clk en
  //   20ish registers
  //   1 OR
  //   3 AND
  //   8 NAND
  //   Note: this allows high loads
endmodule

module ttl74573 (
  input  OEn,
  input  LE,
  input  D0,
  input  D1,
  input  D2,
  input  D3,
  input  D4,
  input  D5,
  input  D6,
  input  D7,
  input  R,
  output O0,
  output O1,
  output O2,
  output O3,
  output O4,
  output O5,
  output O6,
  output O7
);

  wire buffer_1_out, d_ff_1_q, d_ff_2_q, d_ff_3_q, d_ff_4_q, d_ff_5_q, d_ff_6_q, d_ff_7_q, d_ff_8_q,
       not_1_out;

  not not_1 (not_1_out, OEn);
  buf buffer_1 (buffer_1_out, LE);
  D_Flip_Flop d_ff_1 (.D(D0), .clk(buffer_1_out), .Q(d_ff_1_q), .reset(R));  // open: Qn, preset
  D_Flip_Flop d_ff_2 (.D(D1), .clk(buffer_1_out), .Q(d_ff_2_q), .reset(R));  // open: Qn, preset
  D_Flip_Flop d_ff_3 (.D(D2), .clk(buffer_1_out), .Q(d_ff_3_q), .reset(R));  // open: Qn, preset
  D_Flip_Flop d_ff_4 (.D(D3), .clk(buffer_1_out), .Q(d_ff_4_q), .reset(R));  // open: Qn, preset
  D_Flip_Flop d_ff_5 (.D(D4), .clk(buffer_1_out), .Q(d_ff_5_q), .reset(R));  // open: Qn, preset
  D_Flip_Flop d_ff_6 (.D(D5), .clk(buffer_1_out), .Q(d_ff_6_q), .reset(R));  // open: Qn, preset
  D_Flip_Flop d_ff_7 (.D(D6), .clk(buffer_1_out), .Q(d_ff_7_q), .reset(R));  // open: Qn, preset
  D_Flip_Flop d_ff_8 (.D(D7), .clk(buffer_1_out), .Q(d_ff_8_q), .reset(R));  // open: Qn, preset
  assign O0 = not_1_out ? d_ff_1_q : 1'bz;  // Controlled_Buffer controlled_buffer_1
  assign O1 = not_1_out ? d_ff_2_q : 1'bz;  // Controlled_Buffer controlled_buffer_2
  assign O2 = not_1_out ? d_ff_3_q : 1'bz;  // Controlled_Buffer controlled_buffer_3
  assign O3 = not_1_out ? d_ff_4_q : 1'bz;  // Controlled_Buffer controlled_buffer_4
  assign O4 = not_1_out ? d_ff_5_q : 1'bz;  // Controlled_Buffer controlled_buffer_5
  assign O5 = not_1_out ? d_ff_6_q : 1'bz;  // Controlled_Buffer controlled_buffer_6
  assign O6 = not_1_out ? d_ff_7_q : 1'bz;  // Controlled_Buffer controlled_buffer_7
  assign O7 = not_1_out ? d_ff_8_q : 1'bz;  // Controlled_Buffer controlled_buffer_8
endmodule
