// Logisim project pongothree.circ as structural Verilog: 1 circuit, main circuit main
module main (
);

  wire and_1_out, and_2_out, and_3_out, button_1_out, clock_1_out, comparator_1_gt, decoder_1_out0,
       decoder_1_out1, decoder_1_out2, decoder_1_out3, decoder_1_out4, decoder_1_out7, decoder_1_out8,
       decoder_1_out12, decoder_1_out13, decoder_1_out14, decoder_1_out15, not_1_out, or_1_out,
       pull_resistor_1_node, t_ff_1_q, t_ff_1_qn;
  wire [4:0] joystick_1_x, joystick_1_y, rgb_video_1_p4, rgb_video_1_p5;
  wire [7:0] rgb_video_1_p6;
  wire [10:0] adder_1_out, bit_extender_4_out, bit_extender_5_out, Data_q, divider_1_out, divider_1_rem,
       Ip_q, multiplexer_1_out, multiplexer_2_out, nand_1_out, OpA_q, OpB_q, ram_1_dout, RamAddr_q, Test_q,
       TmpA_q, TmpB_q, TmpC_q;
  wire [15:0] Inst_q, rom_1_data;

  Clock clock_1 (.out(clock_1_out));
  Pull_Resistor #(.pull(1)) pull_resistor_1 (.node(pull_resistor_1_node));
  not not_1 (not_1_out, clock_1_out);
  Button button_1 (.out(button_1_out));
  Decoder #(.enable("false"), .select(4)) decoder_1 (
    .out0(decoder_1_out0), .out1(decoder_1_out1), .out2(decoder_1_out2), .out3(decoder_1_out3),
    .out4(decoder_1_out4), .out7(decoder_1_out7), .out8(decoder_1_out8), .out12(decoder_1_out12),
    .out13(decoder_1_out13), .out14(decoder_1_out14), .out15(decoder_1_out15), .sel(Inst_q[4:1]));  // open: out5, out6, out9, out10, out11
  and and_1 (and_1_out, t_ff_1_q, not_1_out);
  T_Flip_Flop t_ff_1 (
    .clk(clock_1_out), .T(pull_resistor_1_node), .Q(t_ff_1_q), .Qn(t_ff_1_qn), .reset(button_1_out));  // open: preset
  and and_2 (and_2_out, t_ff_1_qn, not_1_out);
  or or_1 (or_1_out, decoder_1_out0, and_3_out);
  and and_3 (and_3_out, decoder_1_out1, comparator_1_gt);
  ROM #(.addrWidth(11), .dataWidth(16)) rom_1 (.addr(Ip_q), .data(rom_1_data));
  Counter #(.max('h7ff), .width(11)) Ip (
    .load(or_1_out), .D(Data_q), .Q(Ip_q), .clk(and_1_out), .clr(button_1_out));  // open: count, carry, up
  Register #(.width(11)) Test (.D(Data_q), .en(decoder_1_out2), .Q(Test_q), .clk(and_1_out), .clr(button_1_out));
  RAM #(.addrWidth(11), .dataWidth(11), .enables("line")) ram_1 (
    .addr(RamAddr_q), .we(decoder_1_out8), .clk(and_1_out), .din(Data_q), .dout(ram_1_dout));
  Register #(.width(11)) OpA (.D(Data_q), .en(decoder_1_out3), .Q(OpA_q), .clk(and_1_out), .clr(button_1_out));
  Register #(.width(11)) OpB (.D(Data_q), .en(decoder_1_out4), .Q(OpB_q), .clk(and_1_out), .clr(button_1_out));
  // RGB_Video #(.height(32), .scale(5), .width(32)) rgb_video_1: pin names not known; wires that end beside it: button_1_out, and_1_out, decoder_1_out8, rgb_video_1_p4, rgb_video_1_p5, rgb_video_1_p6
  Bit_Extender #(.in_width(11), .out_width(8)) bit_extender_1 (.in(Data_q), .out(rgb_video_1_p6));
  Bit_Extender #(.in_width(11), .out_width(5)) bit_extender_2 (.in(divider_1_out), .out(rgb_video_1_p5));
  Divider #(.width(11)) divider_1 (.a(RamAddr_q), .b(11'h20), .out(divider_1_out), .rem(divider_1_rem));  // open: upper
  Bit_Extender #(.in_width(11), .out_width(5)) bit_extender_3 (.in(divider_1_rem), .out(rgb_video_1_p4));
  Register #(.width(11)) RamAddr (.D(Data_q), .en(decoder_1_out7), .Q(RamAddr_q), .clk(and_1_out), .clr(button_1_out));
  Register #(.width(11)) TmpA (.D(Data_q), .en(decoder_1_out13), .Q(TmpA_q), .clk(and_1_out), .clr(button_1_out));
  Adder #(.width(11)) adder_1 (.a(OpA_q), .b(OpB_q), .out(adder_1_out));  // open: cin, cout
  Register #(.width(11)) TmpB (.D(Data_q), .en(decoder_1_out14), .Q(TmpB_q), .clk(and_1_out), .clr(button_1_out));
  Register #(.width(11)) TmpC (.D(Data_q), .en(decoder_1_out15), .Q(TmpC_q), .clk(and_1_out), .clr(button_1_out));
  Register #(.width(16)) Inst (.D(rom_1_data), .Q(Inst_q), .clk(and_2_out), .clr(button_1_out));  // open: en
  assign nand_1_out = ~(OpA_q & OpB_q);  // NAND_Gate nand_1, 11 bits wide
  Comparator #(.width(11)) comparator_1 (.a(Test_q), .b({11{1'b0}}), .gt(comparator_1_gt));  // open: eq, lt
  Multiplexer #(.select(4), .width(11)) multiplexer_1 (
    .in0(Ip_q), .in1(Ip_q), .in2(Test_q), .in3(OpA_q), .in4(OpB_q), .in5(adder_1_out), .in6(nand_1_out),
    .in7(RamAddr_q), .in8({11{1'b0}}), .in9(ram_1_dout), .in10(bit_extender_4_out),
    .in11(bit_extender_5_out), .in12({11{1'b0}}), .in13(TmpA_q), .in14(TmpB_q), .in15(TmpC_q),
    .out(multiplexer_1_out), .sel(Inst_q[8:5]));
  Joystick #(.bits(5)) joystick_1 (.x(joystick_1_x), .y(joystick_1_y));
  Multiplexer #(.width(11)) multiplexer_2 (
    .in0(multiplexer_1_out), .in1(Inst_q[15:5]), .out(multiplexer_2_out), .sel(Inst_q[0]));
  assign bit_extender_4_out = {{6{joystick_1_x[4]}}, joystick_1_x};  // Bit_Extender bit_extender_4
  assign bit_extender_5_out = {{6{joystick_1_y[4]}}, joystick_1_y};  // Bit_Extender bit_extender_5
  Register #(.width(11)) Data (.D(multiplexer_2_out), .Q(Data_q), .clk(t_ff_1_q), .clr(button_1_out));  // open: en

  // Notes on the sheet:
  //   contents of rom_1 (hex, n*v repeats v):
  //   800f d1 802f d1 810f d1 812f 511 808f 31 80af 31 804f 211 808f 126 128 c6 29 b0 80cf 151 806f 211
  //   80af 126 128 c6 29 b0 80ef b1 45f 1261 49f 1361 285 ffe9 46 a4 39 4c3 1b 3d 810f 5ff 1781 812f 3dd
  //   67f 1781 6bf 1c61 11 810f 150 812f 170 1ffb 3d 810f 7ff 1781 812f 3dd 87f 1781 80ef 126 ffe9 a4 b0
  //   c03 b1 806f 126 ff89 a4 a03 aa1 126 fc49 a4 aa3 b61 80af 126 128 c6 29 b0 80af 128 806f 126 b0 80cf
  //   126 ffe9 a4 b0 fc3 151 804f 124 de3 800f 126 ffe9 b0 181 126 fc49 a4 e83 f21 802f 126 ffe9 b0 181
  //   808f 128 804f 126 b0 101f 1c61 124 1063 1201 808f 126 128 c6 29 b0 808f 128 804f 126 b0 121f 1c61
  //   1ff1 39 541 7fe5 ffe9 4e 11 46 a4 12a3 1e0 c2f 3c5 1e11 e6 29 ae 46 ffe9 a4 13a3 800f 124 42f 1e11
  //   e6 49 ae 46 ffe9 a4 1503 802f 124 7cf 1e11 e6 ffc9 ae 46 ffe9 a4 1663 1e0 126 89 a6 fca9 a4 1883 64
  //   1981 6e 46 48 c6 29 a8 e6 a4 46 48 a6 68 a6 68 a6 68 a6 68 a6 1c8 ae a5 1b0 e6 409 ae 46 ffe9 a4
  //   1b43 1e0 804f 13a 806f 13c 1c6 1c8 a6 68 a6 68 a6 68 a6 68 a6 1a8 ae 1e0
endmodule
